// Logisim project Circuito_Codice_Gray_Menini_Giorgio.circ as structural Verilog: 2 circuits, main circuit main
module main (
  input  en,
  input  rst,
  output g2,
  output g1,
  output g0
);

  wire ck;

  Clock u_ck (.out(ck));
  // Contatore contatore_1: pin names not known; wires that end beside it: ck, en, rst, g2, g1, g0

  // Notes on the sheet:
  //   SEGNALE
  //   CODIFICA GRAY
endmodule

module Contatore (
  input  ck,
  input  en,
  input  rst,
  output g2,
  output g1,
  output g0
);

  wire and_1_out, and_2_out, and_3_out, and_4_out, and_5_out, or_1_out, or_2_out, s0, s1, s_0, s_1, s_2;

  and and_1 (and_1_out, s_2, s1, s0);
  and and_2 (and_2_out, g2, s_1);
  and and_3 (and_3_out, g2, s_0);
  and and_4 (and_4_out, s_1, s0);
  and and_5 (and_5_out, s1, s_0);
  or or_1 (or_1_out, and_1_out, and_2_out, and_3_out);
  or or_2 (or_2_out, and_4_out, and_5_out);
  D_Flip_Flop d_ff_1 (.clk(ck), .D(or_1_out), .Q(g2), .Qn(s_2), .en(en), .reset(rst));  // open: preset
  D_Flip_Flop d_ff_2 (.clk(ck), .D(or_2_out), .Q(s1), .Qn(s_1), .en(en), .reset(rst));  // open: preset
  D_Flip_Flop d_ff_3 (.clk(ck), .D(s_0), .Q(s0), .Qn(s_0), .en(en), .reset(rst));  // open: preset
  xor xor_1 (g1, g2, s1);
  xor xor_2 (g0, s1, s0);

  // Other names for the same wires on the sheet: s2 = g2

  // Notes on the sheet:
  //   INPUT
  //   CIRCUITO
  //   OUTPUT
endmodule
